# Fritzing sketch Wemos Robot Diagram (saved by Fritzing 0.9.3b)
breadboards: 1

parts:
  J1 = Basic Servo
  VCC1 = 4 x AAA Battery Mount
  WeMos_D1_Mini1 = WeMos D1 Mini  # not connected

nets:
  N1: J1.gnd, VCC1.-
  N2: J1.vcc, VCC1.+
